# Fritzing sketch LW3_Sketch (saved by Fritzing 0.9.3b)

parts:
  Bauteil1 = Arduino Mega 2560 (Rev3)
  RGB_SMD_LED1 = SMD RGB LED (WS2812) [package=5050]
  LED1 = smd LED [color="Red (633nm)" package="0805 [SMD]"]
  R1 = Resistor [tolerance=±5% resistance=220 package="0603 [SMD]"]
  RGB_SMD_LED2 = SMD RGB LED (WS2812) [package=5050]
  RGB_GI = SMD RGB LED (WS2812) [package=5050]
  GND = female pin header, 2 pins [form="♀ (female)"]
  J2 = female pin header, 2 pins [form="♀ (female)"]
  J3 = female pin header, 2 pins [form="♀ (female)"]
  CN10 = female pin header, 2 pins [form="♀ (female)"]
  J5 = female pin header, 2 pins [form="♀ (female)"]
  J6 = female pin header, 2 pins [form="♀ (female)"]
  J7 = female pin header, 2 pins [form="♀ (female)"]  # not connected
  J8 = female pin header, 2 pins [form="♀ (female)"]  # not connected
  J9 = female pin header, 2 pins [form="♀ (female)"]  # not connected
  J10 = female pin header, 2 pins [form="♀ (female)"]  # not connected
  CN8 = female pin header, 2 pins [form="♀ (female)"]
  VCC1 = 4 x AAA Battery Mount
  RGB_FLFI_Left = SMD RGB LED (WS2812) [package=5050]
  RGB_FLIFI_Right = SMD RGB LED (WS2812) [package=5050]

nets:
  VSS: Bauteil1.GND, RGB_SMD_LED1.VSS, R1.Pin_1, RGB_SMD_LED2.VSS, RGB_GI.VSS, GND.pin2, VCC1.-, RGB_FLFI_Left.VSS, RGB_FLIFI_Right.VSS
  N1: Bauteil1.D13_PWM, LED1.anode
  N2: Bauteil1.D12_PWM, RGB_SMD_LED1.DIn
  N3: Bauteil1.D11_PWM, RGB_FLFI_Left.DIn
  N4: Bauteil1.D10_PWM, RGB_FLIFI_Right.DIn
  VDD: Bauteil1.5V, RGB_SMD_LED1.VDD, RGB_SMD_LED2.VDD, RGB_GI.VDD, VCC1.+, RGB_FLFI_Left.VDD, RGB_FLIFI_Right.VDD
  N5: Bauteil1.D2_PWM, CN8.pin1
  N6: Bauteil1.D22, J6.pin1
  N7: Bauteil1.D23, J6.pin2
  N8: Bauteil1.D24, J5.pin2
  N9: Bauteil1.D25, J2.pin1
  N10: Bauteil1.D26, J2.pin2
  N11: Bauteil1.D27, J3.pin2
  N12: Bauteil1.D28, CN10.pin1
  N13: Bauteil1.D29, CN10.pin2
  N14: RGB_SMD_LED1.DOut, RGB_SMD_LED2.DIn
  N15: RGB_SMD_LED2.DOut, RGB_GI.DIn

notes:
  GI: 36 LEDs
  FLIFI Left: 4 LEDs
  FLIFI Right: 4 LEDs
  Switching Power Supply
  5V / 6A
